# Fritzing sketch shield (saved by Fritzing 0.7.11b)
breadboards: 1

parts:
  R1 = Resistor [tolerance=±5% resistance=220 package=THT]
  R2 = Resistor [tolerance=±5% resistance=2.2k package=THT]
  R3 = Resistor [tolerance=±5% resistance=47k package=THT]
  U1 = Optocoupler [package=THT]
  Shutter = Pushbutton [package="[THT]"]
  Arduino1 = Arduino
  Q1 = Basic FET N-Channel [package="TO220 [THT]"]
  R4 = Resistor [tolerance=±5% resistance=2.2k package=THT]
  Valve = Pushbutton [package="[THT]"]
  PCB1 = Arduino Shield PCB [sticky=true]  # not connected
  Valve_2 = female pin header, 3 pins [form="♀ (female)"]
  12V = female pin header, 3 pins [form="♀ (female)"]
  Camera = female pin header, 3 pins [form="♀ (female)"]

nets:
  N1: R1.Pin_0, Arduino1.D13
  N2: R1.Pin_1, U1.Pin_1
  N3: R2.Pin_0, R3.Pin_1, U1.Pin_4, Shutter.Pin_1, Shutter.Pin_2
  N4: R2.Pin_1, Camera.pin3
  N5: R3.Pin_0, U1.Pin_5, Shutter.Pin_3, Shutter.Pin_4, Camera.pin2
  N6: U1.Pin_2, Arduino1.GND, Q1.source, Valve.Pin_1, Valve.Pin_2, 12V.pin2
  N7: Arduino1.D12, R4.Pin_0
  N8: Q1.gate, R4.Pin_1
  N9: Q1.drain, Valve.Pin_3, Valve.Pin_4, Valve_2.pin1
  N10: Valve_2.pin2, Valve_2.pin3, 12V.pin1

custom parts:
  Arduino Shield PCB: Plain PCB Shaped to fit an Arduino "Shield"
